# Fritzing sketch esquematico (saved by Fritzing 0.8.5b)
circuit board: 8.46667cm x 5.64444cm
breadboards: 1

parts:
  R3 = Resistor [tolerance=±5% resistance=10k package=THT]
  22pF = Capacitor [package=cap-pth-small2]
  16MHz = CRYSTAL [package=hc49us]
  5V = Pushbutton [package="[THT]"]
  22pF_2 = Capacitor [package=cap-pth-small2]
  U1 = atmega328 [package=dip]
  R4 = Resistor [tolerance=±5% resistance=220 package=THT]
  7805 = Voltage Regulator - 5V [package="DPak [SMD]"]
  TIP41C = npn-Powertransistor [package="TO220 [THT]"]
  TIP41C_2 = npn-Powertransistor [package="TO220 [THT]"]
  TIP41C_3 = npn-Powertransistor [package="TO220 [THT]"]
  R5 = Resistor [tolerance=±5% resistance=330 package=THT]
  R6 = Resistor [tolerance=±5% resistance=330 package=THT]
  R7 = Resistor [tolerance=±5% resistance=330 package=THT]
  12V = Battery Holders [package=battery_20mm_pth_compact]  # not connected
  LED1 = LED - 5mm [color="Orange (620nm)" package="5 mm [THT]"]

nets:
  N1: R3.Pin_0, U1.VCC, U1.AVCC, U1.AREF, 7805.output_voltage
  N2: R3.Pin_1, 5V.Pin_1, 5V.Pin_2, U1.RESET
  N3: 22pF.1, 16MHz.2, U1.XLAT2
  N4: 22pF.2, 5V.Pin_3, 5V.Pin_4, 22pF_2.1, U1.GND, R4.Pin_1, TIP41C.emitter, TIP41C_2.emitter, TIP41C_3.emitter
  N5: 16MHz.1, 22pF_2.2, U1.XLAT1
  N6: U1.D5_(PWM), LED1.anode
  N7: U1.D6_(PWM), R7.Pin_0
  N8: U1.D9_(PWM), R5.Pin_0
  N9: U1.D10_(PWM), R6.Pin_0
  N10: R4.Pin_0, LED1.cathode
  N11: TIP41C.base, R5.Pin_1
  N12: TIP41C_2.base, R6.Pin_1
  N13: TIP41C_3.base, R7.Pin_1
