# Fritzing sketch esquematico (saved by Fritzing 0.8.5b)
breadboards: 1

parts:
  LED2 = LED - 5mm [color="Red (633nm)" package="5 mm [THT]"]
  R5 = Resistor [tolerance=±5% resistance=220 package=THT]
  U5 = atmega328 [package=dip]
  R6 = Resistor [tolerance=±5% resistance=10k package=THT]
  22pF = Capacitor [package=cap-pth-small2]
  22pF_2 = Capacitor [package=cap-pth-small2]
  S2 = Pushbutton [package="[THT]"]
  5V = Voltage Regulator - 5V [package="TO220 [THT]"]
  12V = Battery Holders [package=battery_20mm_pth_compact]  # not connected
  TIP41C = npn-Powertransistor [package="TO220 [THT]"]
  Q2 = npn-Powertransistor [package="TO220 [THT]"]
  Q3 = npn-Powertransistor [package="TO220 [THT]"]
  R7 = Resistor [tolerance=±5% resistance=330 package=THT]
  R8 = Resistor [tolerance=±5% resistance=330 package=THT]
  R9 = Resistor [tolerance=±5% resistance=330 package=THT]
  16MHz = CRYSTAL [package=hc49us]
  LED3 = RGB LED (com. anode, rbg) [package="5 mm [THT]"]
  Parte1 = Breakout Board for Electret Microphone

nets:
  N1: LED2.cathode, R5.Pin_0
  N2: LED2.anode, U5.D5_(PWM)
  GND: R5.Pin_1, U5.GND, 22pF.1, 22pF_2.2, S2.Pin_3, S2.Pin_4, 5V.GND, TIP41C.emitter, Q2.emitter, Q3.emitter, Parte1.GND
  N3: U5.RESET, R6.Pin_1, S2.Pin_1, S2.Pin_2
  VCC: U5.VCC, U5.AVCC, U5.AREF, R6.Pin_0, 5V.output_voltage, Parte1.VCC
  N4: U5.XLAT1, 22pF.2, 16MHz.1
  N5: U5.XLAT2, 22pF_2.1, 16MHz.2
  N6: U5.D6_(PWM), R9.Pin_1
  N7: U5.D9_(PWM), R7.Pin_1
  N8: U5.D10_(PWM), R8.Pin_1
  N9: U5.A5, Parte1.AUD
  N10: 5V.input_voltage, LED3.red_cathode
  N11: TIP41C.base, R7.Pin_0
  N12: TIP41C.collector, LED3.green_cathode
  N13: Q2.base, R8.Pin_0
  N14: Q2.collector, LED3.blue_cathode
  N15: Q3.base, R9.Pin_0
  N16: Q3.collector, LED3.common_anode
